// Logisim project cpu.circ as structural Verilog
module register_file (
  input  [3:0] RD2,
  input  [3:0] RD1,
  input  [31:0] in_3,
  input  in_4,
  input  [31:0] in_5,
  input  [3:0] WRN,
  input  in_7,
  output [31:0] out_8,
  output [31:0] out_9,
  output [31:0] out_10,
  output [31:0] out_11,
  output [31:0] out_12,
  output [31:0] out_13,
  output [31:0] RV2,
  output [31:0] out_15,
  output [31:0] out_16,
  output [31:0] out_17,
  output [31:0] out_18,
  output [31:0] out_19,
  output [31:0] out_20,
  output [31:0] out_21,
  output [31:0] out_22,
  output [31:0] out_23,
  output [31:0] out_24,
  output [31:0] out_25,
  output [31:0] RV1,
  output [31:0] CPSR
);

  wire CLK, LR_WE, PC_WE, R0_WE, R1_WE, R2_WE, R3_WE, R4_WE, R5_WE, R6_WE, R7_WE, R8_WE, R9_WE, R10_WE,
       R11_WE, R12_WE, SP_WE;

  Clock clock_1 (.out(CLK));
  Register #(.width(32), .trigger("falling")) register_1 (.D(in_3), .en(R0_WE), .Q(out_8), .clk(CLK), .clr(in_4));
  Register #(.width(32), .trigger("falling")) register_2 (.D(in_3), .en(R1_WE), .Q(out_15), .clk(CLK), .clr(in_4));
  Register #(.width(32), .trigger("falling")) register_3 (.D(in_3), .en(R2_WE), .Q(out_21), .clk(CLK), .clr(in_4));
  Register #(.width(32), .trigger("falling")) register_4 (.D(in_3), .en(R3_WE), .Q(out_9), .clk(CLK), .clr(in_4));
  Register #(.width(32), .trigger("falling")) register_5 (.D(in_3), .en(R4_WE), .Q(out_16), .clk(CLK), .clr(in_4));
  Register #(.width(32), .trigger("falling")) register_6 (.D(in_3), .en(R5_WE), .Q(out_22), .clk(CLK), .clr(in_4));
  Register #(.width(32), .trigger("falling")) register_7 (.D(in_3), .en(R6_WE), .Q(out_10), .clk(CLK), .clr(in_4));
  Register #(.width(32), .trigger("falling")) register_8 (.D(in_3), .en(R7_WE), .Q(out_17), .clk(CLK), .clr(in_4));
  Register #(.width(32), .trigger("falling")) register_9 (.D(in_3), .en(R8_WE), .Q(out_23), .clk(CLK), .clr(in_4));
  Decoder #(.select(4), .enable("false")) decoder_1 (
    .out0(R0_WE), .out1(R1_WE), .out2(R2_WE), .out3(R3_WE), .out4(R4_WE), .out5(R5_WE), .out6(R6_WE),
    .out7(R7_WE), .out8(R8_WE), .out9(R9_WE), .out10(R10_WE), .out11(R11_WE), .out12(R12_WE), .out13(SP_WE),
    .out14(LR_WE), .out15(PC_WE), .sel(WRN));
  Register #(.width(32), .trigger("falling")) register_10 (.D(in_3), .en(R9_WE), .Q(out_11), .clk(CLK), .clr(in_4));
  Register #(.width(32), .trigger("falling")) register_11 (.D(in_3), .en(R10_WE), .Q(out_18), .clk(CLK), .clr(in_4));
  Register #(.width(32), .trigger("falling")) register_12 (.D(in_3), .en(R11_WE), .Q(out_24), .clk(CLK), .clr(in_4));
  Register #(.width(32), .trigger("falling")) register_13 (.D(in_3), .en(R12_WE), .Q(out_12), .clk(CLK), .clr(in_4));
  Register #(.width(32), .trigger("falling")) register_14 (.D(in_3), .en(SP_WE), .Q(out_19), .clk(CLK), .clr(in_4));
  Register #(.width(32), .trigger("falling")) register_15 (.D(in_3), .en(LR_WE), .Q(out_25), .clk(CLK), .clr(in_4));
  Register #(.width(32), .trigger("falling")) register_16 (.D(in_3), .en(PC_WE), .Q(out_13), .clk(CLK), .clr(in_4));
  Register #(.width(32), .trigger("falling")) register_17 (.D(in_5), .en(in_7), .Q(CPSR), .clk(CLK), .clr(in_4));
  Multiplexer #(.select(4), .width(32), .enable("false")) multiplexer_1 (
    .in0(out_8), .in1(out_15), .in2(out_21), .in3(out_9), .in4(out_16), .in5(out_22), .in6(out_10),
    .in7(out_17), .in8(out_23), .in9(out_11), .in10(out_18), .in11(out_24), .in12(out_12), .in13(out_19),
    .in14(out_25), .in15(out_13), .out(RV2), .sel(RD2));
  Multiplexer #(.select(4), .width(32), .enable("false")) multiplexer_2 (
    .in0(out_8), .in1(out_15), .in2(out_21), .in3(out_9), .in4(out_16), .in5(out_22), .in6(out_10),
    .in7(out_17), .in8(out_23), .in9(out_11), .in10(out_18), .in11(out_24), .in12(out_12), .in13(out_19),
    .in14(out_25), .in15(out_13), .out(RV1), .sel(RD1));

  assign out_20 = CPSR;

  // Other names for the same wires on the sheet: CLR = in_4; CPSR_IN[31:0] = in_5; CPSR_Q[31:0] = CPSR;
  //   CPSR_WE = in_7; LR_Q[31:0] = out_25; PC_Q[31:0] = out_13; R0_Q[31:0] = out_8; R1_Q[31:0] = out_15;
  //   R2_Q[31:0] = out_21; R3_Q[31:0] = out_9; R4_Q[31:0] = out_16; R5_Q[31:0] = out_22; R6_Q[31:0] = out_10;
  //   R7_Q[31:0] = out_17; R8_Q[31:0] = out_23; R9_Q[31:0] = out_11; R10_Q[31:0] = out_18; R11_Q[31:0] = out_24;
  //   R12_Q[31:0] = out_12; SP_Q[31:0] = out_19; WD[31:0] = in_3
endmodule
